# Fritzing sketch ServerusNebulizador (saved by Fritzing 0.9.3b)

parts:
  Componente1 = FTDI Basic Programmer
  U1 = ESP8266 WiFi Module [part_number=ESP8266]
  JP1 = Header 4 [package=molex-1x4_lock]
  U2 = Voltage Regulator - 3.3V [package="TO220 [THT]"]
  U4 = RELAY [package=relay-g5q]
  Q1 = NPN-Transistor [package="SOT-23 [SMD]"]
  S1 = Pushbutton [package="[THT]"]
  S2 = Pushbutton [package="[THT]"]
  S3 = Pushbutton [package="[THT]"]
  J1 = Power Jack [package=power_jack_slot]
  M1 = RioRand LM2596
  DHT1 = DHT11 Humitidy and Temperature Sensor
  KY-1 = Keyes Relay [package=THT]
  R1 = Resistor [tolerance=±5% resistance=10k package=THT]
  R2 = Resistor [tolerance=±5% resistance=10k package=THT]
  R3 = Resistor [tolerance=±5% resistance=10k package=THT]
  R4 = Resistor [tolerance=±5% resistance=4.7k package=THT]
  J2 = Camdenboss CTB0158-2 [part_number=CTB0158-2 package=THT]
  J3 = Camdenboss CTB0158-2 [part_number=CTB0158-2 package=THT]
  J5 = Camdenboss CTB0158-3 [part_number=CTB0158-3 package=THT]  # not connected

nets:
  N1: Componente1.RXI, U1.RXD, JP1.2
  N2: Componente1.TXO, U1.TXD, JP1.3
  N3: Componente1.POWER, JP1.4, U2.input_voltage
  N4: Componente1.GND, JP1.1
  N5: U1.GPIO_0, S2.Pin_3, S2.Pin_4
  N6: U1.GPIO_2, R1.Pin_0
  N7: U1.CH_PD, R3.Pin_0
  N8: U1.GPIO_15, R2.Pin_0
  N9: U1.GPIO_4, S3.Pin_3, S3.Pin_4
  N10: U1.GPIO_5, Q1.0
  N11: U1.REST, S1.Pin_2
  N12: U4.MAIN, J2.pin2
  N13: U4.NO, J2.pin1
  N14: U4.COIL1, Q1.2
  N15: J1.GND, M1.Pin_2
  N16: J1.PWR, M1.Pin_1
  N17: DHT1.DATA, R4.Pin_1
  N18: KY-1.NO, J3.pin1

notes:
  Serverus (ESP-07)
  Modificado para nebulizador
  SW1
  reset
  SW2
  GPIO0
  SW3
  GPIO4
  Entrada 12V - Salida 5V
  Regulador a 3.3V
  DHT11,
  DHT22 o
  DS18B20
  GPIO14
  Relay o MOSFET
  GPIO12
  GPIO2
  LED
  12V

custom parts:
  DHT11 Humitidy and Temperature Sensor: DHT11 Humidity and Temperature Sensor
  Keyes Relay: The Keyes 5V relay module is suitable for SCM development, home appliance control. It uses a 5V~12V TIL control signal which can control DC / AC signal.
