# Fritzing sketch Serverus (saved by Fritzing 0.9.3b)

parts:
  Componente1 = FTDI Basic Programmer
  U1 = ESP8266 WiFi Module [part_number=ESP8266]
  JP1 = Header 4 [package=molex-1x4_lock]
  U2 = Voltage Regulator - 3.3V [package="TO220 [THT]"]
  U4 = RELAY [package=relay-g5q]
  Q1 = NPN-Transistor [package="SOT-23 [SMD]"]
  S1 = Pushbutton [package="[THT]"]
  S2 = Pushbutton [package="[THT]"]
  S3 = Pushbutton [package="[THT]"]

nets:
  N1: Componente1.RXI, U1.RXD, JP1.2
  N2: Componente1.TXO, U1.TXD, JP1.3
  N3: Componente1.POWER, JP1.4, U2.input_voltage
  N4: Componente1.GND, JP1.1
  N5: U1.GPIO_0, S2.Pin_3, S2.Pin_4
  N6: U1.GPIO_4, S3.Pin_3, S3.Pin_4
  N7: U1.GPIO_5, Q1.0
  N8: U1.REST, S1.Pin_2
  N9: U4.COIL1, Q1.2

notes:
  Serverus (ESP-07)
  SW1
  reset
  SW2
  GPIO0
  SW3
  GPIO4
